// Logisim project ual tp 1.circ as structural Verilog: 3 circuits, main circuit main
module main (
  input  a,
  input  b,
  output out_3
);

  xnor xnor_1 (out_3, a, b);
endmodule

module _4bit_comparateur (
  input  [3:0] in_1,
  input  [3:0] in_2,
  output out_3
);

  wire main_1_out_3, main_2_out_3, main_3_out_3, main_4_out_3;

  main main_1 (.a(in_1[0]), .b(in_2[0]), .out_3(main_1_out_3));
  main main_2 (.a(in_1[1]), .b(in_2[1]), .out_3(main_2_out_3));
  main main_3 (.a(in_1[2]), .b(in_2[2]), .out_3(main_3_out_3));
  main main_4 (.a(in_1[3]), .b(in_2[3]), .out_3(main_4_out_3));
  and and_1 (out_3, main_1_out_3, main_2_out_3, main_3_out_3, main_4_out_3);
endmodule

module ual (
  input  [3:0] a,
  input  [3:0] b,
  input  [2:0] operator_code,
  output [2:0] registre_d_etat,
  output [3:0] \output 
);

  wire adder_1_cout, subtractor_1_bout;
  wire [3:0] adder_1_out, and_1_out, not_1_out, not_2_out, or_1_out, subtractor_1_out, xor_1_out;

  Adder #(.width(4)) adder_1 (.a(a), .b(b), .out(adder_1_out), .cin(1'b0), .cout(adder_1_cout));
  Subtractor #(.width(4)) subtractor_1 (.a(a), .b(b), .out(subtractor_1_out), .bin(1'b0), .bout(subtractor_1_bout));
  assign and_1_out = a & b;  // AND_Gate and_1, 4 bits wide
  assign or_1_out = a | b;  // OR_Gate or_1, 4 bits wide
  assign xor_1_out = a ^ b;  // XOR_Gate xor_1, 4 bits wide
  assign not_1_out = ~a;  // NOT_Gate not_1, 4 bits wide
  assign not_2_out = ~b;  // NOT_Gate not_2, 4 bits wide
  Multiplexer #(.select(3), .width(4), .enable("false")) multiplexer_1 (
    .in0(not_2_out), .in1(adder_1_out), .in2(subtractor_1_out), .in4(and_1_out), .in5(or_1_out),
    .in6(xor_1_out), .in7(not_1_out), .out(\output ), .sel(operator_code));  // open: in3
  Multiplexer #(.enable("false")) multiplexer_2 (
    .in0(adder_1_cout), .in1(subtractor_1_bout), .out(registre_d_etat[0]));  // open: sel
  nor nor_1 (registre_d_etat[1], \output [0], \output [1], \output [2], \output [3]);

  assign registre_d_etat[2] = \output [3];
endmodule
